# Fritzing sketch FlipDot34 (saved by Fritzing 0.9.6b)
breadboards: 1

parts:
  Part1 = Arduino Nano (Rev3.0)
  J1 = shrouded pin header, 34 pins [form="♂ (shrouded male)"]
  U1 = 74HC595 [package="DIP16 [THT]"]
  U2 = 74HC595 [package="DIP16 [THT]"]
  C1 = Ceramic Capacitor [capacitance="100 nF" voltage=35V package="1206 [SMD, multilayer]"]
  C2 = Ceramic Capacitor [capacitance="100 nF" voltage=35V package="0805 [SMD, multilayer]"]
  J2 = Power Jack [package=power_jack_combo]

nets:
  GND: Part1.GND, J1.pin1, J1.pin2, J1.pin16, J1.pin17, J1.pin18, J1.pin19, J1.pin33, J1.pin34, U1.GND, U1.OE, U2.GND, U2.OE, C1.0, C2.0, J2.GND
  N1: Part1.D2, J1.pin28
  N2: Part1.D3, J1.pin27
  N3: Part1.D4, J1.pin26
  N4: Part1.D5, J1.pin25
  N5: Part1.D6, J1.pin24
  N6: Part1.D7, J1.pin23
  N7: Part1.D9, U1.ST_CP, U2.ST_CP
  N8: Part1.D10, U1.DS
  N9: Part1.D11/MOSI, U1.SH_CP, U2.SH_CP
  VCC: Part1.5V, J1.pin32, U1.MR, U1.VCC, U2.MR, U2.VCC, C1.1, C2.1
  N10: J1.pin4, U2.Q3
  N11: J1.pin5, U2.Q4
  N12: J1.pin6, U2.Q5
  N13: J1.pin7, U2.Q6
  N14: J1.pin8, U2.Q7
  N15: J1.pin9, U1.Q1
  N16: J1.pin10, U1.Q2
  N17: J1.pin11, U1.Q3
  N18: J1.pin12, U1.Q4
  N19: J1.pin13, U1.Q5
  N20: J1.pin15, J2.PWR
  N21: J1.pin29, U2.Q1
  N22: J1.pin30, U2.Q2
  N23: J1.pin31, U2.Q0
  N24: U1.Q7', U2.DS

notes:
  24 V
